# Fritzing sketch mindstorms (saved by Fritzing 0.9.9b)
breadboards: 1

parts:
  U1 = ESP32S-HiLetgo [part_number=ESP32S-HiLetgo]
  IC1 = L293D [package=THT]
  J1 = female pin header, 6 pins [form="♀ (female)"]
  J2 = female pin header, 6 pins [form="♀ (female)"]
  LED1 = smd LED [color="Red (633nm)" package="0805 [SMD]"]
  LED2 = smd LED [color="Green (565nm)" package="0805 [SMD]"]
  LED3 = smd LED [color="Red (633nm)" package="0805 [SMD]"]
  LED5 = smd LED [color="Green (565nm)" package="0805 [SMD]"]
  R1 = Resistor [tolerance=±5% power=0.25 resistance=220 package=THT]
  R2 = Resistor [tolerance=±5% power=0.25 resistance=220 package=THT]
  IC2 = Voltage Regulator [package=to-220-alt]
  J3 = Power Jack [package=power_jack_smd]
  C1 = Capacitor Polarized [package=cpol-radial-10uf-25v]

nets:
  N1: U1.EN, C1.-
  N2: U1.GPIO32, J2.pin6
  N3: U1.GPIO33, J2.pin5
  N4: U1.GND, IC1.0V, J1.pin4, J2.pin3, IC2.IN, J3.GNDBREAK, C1.+
  N5: U1.VIN, IC1.+V, J1.pin3, J2.pin4
  N6: U1.GPIO15, IC1.In_4
  N7: U1.GPIO16, J1.pin1
  N8: U1.GPIO17, J1.pin2
  N9: U1.GPIO18, IC1.In_3
  N10: U1.GPIO21, IC1.Enable_2
  N11: U1.GPIO22, IC1.Enable_1
  N12: U1.GPIO23, IC1.In_1
  N13: IC1.Out_1_(_Controlled_by_Enable_1_), J1.pin6, R1.Pin_1
  N14: IC1.Out_2_(_Controlled_by_Enable_1_), J1.pin5, LED1.cathode, LED2.anode
  N15: IC1.+Vmotor, IC2.OUT
  N16: IC1.Out_3_(_Controlled_by_Enable_2_), J2.pin2, LED3.cathode, LED5.anode
  N17: IC1.Out_4_(_Controlled_by_Enable_2_), J2.pin1, R2.Pin_1
  N18: LED1.anode, LED2.cathode, R1.Pin_0
  N19: LED3.anode, LED5.cathode, R2.Pin_0
  GND: IC2.GND, J3.GND

custom parts:
  ESP32S-HiLetgo: HiLetgo ESP-WROOM-32 ESP32 ESP-32S Development Board 2.4GHz Dual-Mode WiFi + Bluetooth Dual Cores Microcontroller The ESP32 integrated with Antenna switches, RF Balun, power amplifiers, low-noise amplifiers, filters, and management modules, and the entire solution occupies the least area of PCB. 2.4 GHz Wi-Fi plus Bluetooth dual-mode chip, with TSMC Ultra-low power consumption 40nm technology,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
